# Fritzing sketch pawsfzz (saved by Fritzing 0.9.6b)
breadboards: 1

parts:
  uPesy_ESP32_Wrover_DevKit1 = uPesy ESP32 Wrover DevKit v2
  Composant1 = Barometric Pressure Sensor - BMP180 Breakout (GY-68)
  ZS-042_RTC1 = ZS-042 RTC Module
  S1 = Pushbutton [package="[THT]"]
  R1 = Resistor [tolerance=±5% power=0.25 resistance=220 package=THT]
  microSD1 = MicroSD Card Module

nets:
  N1: uPesy_ESP32_Wrover_DevKit1.GPIO22, Composant1.SCL, ZS-042_RTC1.SCL
  N2: uPesy_ESP32_Wrover_DevKit1.GPIO21, Composant1.SDA, ZS-042_RTC1.SDA
  N3: uPesy_ESP32_Wrover_DevKit1.GPIO5, microSD1.CS
  VCC: uPesy_ESP32_Wrover_DevKit1.3V3, Composant1.VCC, ZS-042_RTC1.VCC, R1.Pin_1, microSD1.VCC
  GND: uPesy_ESP32_Wrover_DevKit1.GND#16, Composant1.GND, ZS-042_RTC1.GND, microSD1.GND
  N4: uPesy_ESP32_Wrover_DevKit1.GPIO39, S1.Pin_1, S1.Pin_2, R1.Pin_0
  N5: uPesy_ESP32_Wrover_DevKit1.GPIO36, ZS-042_RTC1.SQW
  N6: S1.Pin_3, S1.Pin_4

custom parts:
  uPesy ESP32 Wrover DevKit v2: ESP32 development board that is 100% breadboard compatible with 4MB PSRAM and USB-C connector
